// Logisim project P0_L0_CRC.circ as structural Verilog: 3 circuits, main circuit 4:4XDividor
module _4_4XDividor (
  input  [3:0] divident,
  input  [3:0] divisor,
  output [2:0] remainder
);

  wire [2:0] xor_3_out;

  xor xor_1 (xor_3_out[2], divident[2], divisor[2]);
  xor xor_2 (xor_3_out[1], divident[1], divisor[1]);
  xor xor_3 (xor_3_out[0], divident[0], divisor[0]);
  Multiplexer #(.width(3)) multiplexer_1 (
    .in0(divident[2:0]), .in1(xor_3_out), .out(remainder), .sel(divident[3]));  // open: en
endmodule

module CRC (
  input  [3:0] B,
  input  [7:0] A,
  output [10:0] C
);

  wire [3:1] n4_4xdividor_1_remainder, n4_4xdividor_2_remainder, n4_4xdividor_3_remainder,
       n4_4xdividor_4_remainder, n4_4xdividor_5_remainder, n4_4xdividor_6_remainder, n4_4xdividor_7_remainder;

  _4_4XDividor u_4_4xdividor_1 (.divident(A[7:4]), .divisor(B), .remainder(n4_4xdividor_1_remainder));
  _4_4XDividor u_4_4xdividor_2 (
    .divident({n4_4xdividor_1_remainder, A[3]}), .divisor(B), .remainder(n4_4xdividor_2_remainder));
  _4_4XDividor u_4_4xdividor_3 (
    .divident({n4_4xdividor_2_remainder, A[2]}), .divisor(B), .remainder(n4_4xdividor_3_remainder));
  _4_4XDividor u_4_4xdividor_4 (
    .divident({n4_4xdividor_3_remainder, A[1]}), .divisor(B), .remainder(n4_4xdividor_4_remainder));
  _4_4XDividor u_4_4xdividor_5 (
    .divident({n4_4xdividor_4_remainder, A[0]}), .divisor(B), .remainder(n4_4xdividor_5_remainder));
  _4_4XDividor u_4_4xdividor_6 (
    .divident({n4_4xdividor_5_remainder, 1'b0}), .divisor(B), .remainder(n4_4xdividor_6_remainder));
  _4_4XDividor u_4_4xdividor_7 (
    .divident({n4_4xdividor_6_remainder, 1'b0}), .divisor(B), .remainder(n4_4xdividor_7_remainder));
  _4_4XDividor u_4_4xdividor_8 (.divident({n4_4xdividor_7_remainder, 1'b0}), .divisor(B), .remainder(C[2:0]));

  assign C[10:3] = A;
endmodule

module Main (
  input  [7:0] in_1,
  input  [3:0] in_2,
  output [10:0] out_3
);

  CRC crc_1 (.B(in_2), .A(in_1), .C(out_3));
endmodule
