// Logisim project P0_L0_FSM.circ as structural Verilog: 3 circuits, main circuit fsm
module fsm (
  input  CLR,
  input  [1:0] In,
  output Z
);

  wire CLK;
  wire [2:0] multiplexer_1_out, register_1_q, statetransition_1_statenew;

  Clock clock_1 (.out(CLK));
  stateTransition statetransition_1 (.stateOld(register_1_q), .In(In), .stateNew(statetransition_1_statenew));
  Multiplexer #(.width(3)) multiplexer_1 (
    .in0(statetransition_1_statenew), .in1(3'b000), .out(multiplexer_1_out), .sel(CLR));  // open: en
  Register #(.width(3)) register_1 (.D(multiplexer_1_out), .Q(register_1_q), .clk(CLK));  // open: en, clr
  outputCalculation outputcalculation_1 (.state(register_1_q), .In(In), .Z(Z));
endmodule

module stateTransition (
  input  [2:0] stateOld,
  input  [1:0] In,
  output [2:0] stateNew
);

  wire and_2_out, and_3_out, and_4_out, and_5_out, and_6_out, and_7_out, and_8_out, and_9_out, not_1_out,
       not_2_out, not_3_out, not_4_out, not_5_out, not_6_out, not_7_out, not_8_out, not_9_out, not_10_out,
       not_11_out, not_12_out, not_13_out, not_14_out, not_15_out, not_16_out, not_17_out, not_18_out,
       not_19_out, not_20_out, not_21_out, not_22_out, not_23_out, not_24_out, not_25_out;

  not not_1 (not_1_out, stateOld[2]);
  not not_2 (not_2_out, In[0]);
  not not_3 (not_3_out, stateOld[2]);
  not not_4 (not_4_out, stateOld[1]);
  not not_5 (not_5_out, In[1]);
  not not_6 (not_6_out, stateOld[2]);
  not not_7 (not_7_out, stateOld[1]);
  not not_8 (not_8_out, In[0]);
  not not_9 (not_9_out, stateOld[2]);
  not not_10 (not_10_out, stateOld[0]);
  not not_11 (not_11_out, In[1]);
  not not_12 (not_12_out, stateOld[2]);
  not not_13 (not_13_out, stateOld[0]);
  not not_14 (not_14_out, In[0]);
  not not_15 (not_15_out, stateOld[1]);
  not not_16 (not_16_out, stateOld[0]);
  not not_17 (not_17_out, In[1]);
  not not_18 (not_18_out, stateOld[2]);
  not not_19 (not_19_out, stateOld[1]);
  not not_20 (not_20_out, In[0]);
  not not_21 (not_21_out, stateOld[2]);
  not not_22 (not_22_out, stateOld[0]);
  not not_23 (not_23_out, In[0]);
  not not_24 (not_24_out, stateOld[2]);
  not not_25 (not_25_out, In[1]);
  and and_1 (stateNew[2], not_1_out, stateOld[1], stateOld[0], not_2_out);
  and and_2 (and_2_out, not_3_out, not_4_out, stateOld[0], not_5_out);
  and and_3 (and_3_out, not_6_out, not_7_out, stateOld[0], not_8_out);
  and and_4 (and_4_out, not_9_out, stateOld[1], not_10_out, not_11_out);
  and and_5 (and_5_out, not_12_out, stateOld[1], not_13_out, not_14_out);
  and and_6 (and_6_out, not_15_out, not_16_out, not_17_out, In[0]);
  and and_7 (and_7_out, not_18_out, not_19_out, stateOld[0], not_20_out);
  and and_8 (and_8_out, not_21_out, stateOld[1], not_22_out, not_23_out);
  and and_9 (and_9_out, not_24_out, stateOld[1], stateOld[0], not_25_out, In[0]);
  or or_1 (stateNew[1], and_2_out, and_3_out, and_4_out, and_5_out);
  or or_2 (stateNew[0], and_6_out, and_7_out, and_8_out, and_9_out);
endmodule

module outputCalculation (
  input  [2:0] state,
  input  [1:0] In,
  output Z
);

  wire not_1_out, not_2_out;

  not not_1 (not_1_out, state[2]);
  not not_2 (not_2_out, In[0]);
  and and_1 (Z, not_1_out, state[1], state[0], not_2_out);
endmodule
