// Logisim project P0_L0_GRF.circ as structural Verilog: 1 circuit, main circuit grf
module grf (
  input  clk,
  input  reset,
  input  WE,
  input  [4:0] A1,
  input  [4:0] A2,
  input  [4:0] A3,
  input  [31:0] WD,
  output [31:0] RD1,
  output [31:0] RD2
);

  wire _0, _1, _2, _3, _4, _5, _6, _7, _8, _9, _10, _11, _12, _13, _14, _15, _16, _17, _18, _19, _20, _21,
       _22, _23, _24, _25, _26, _27, _28, _29, _30, _31, and_1_out, and_2_out, and_3_out, and_4_out,
       and_5_out, and_6_out, and_7_out, and_8_out, and_9_out, and_10_out, and_11_out, and_12_out, and_13_out,
       and_14_out, and_15_out, and_16_out, and_17_out, and_18_out, and_19_out, and_20_out, and_21_out,
       and_22_out, and_23_out, and_24_out, and_25_out, and_26_out, and_27_out, and_28_out, and_29_out,
       and_30_out, and_31_out, and_32_out;
  wire [31:0] O0, O1, O2, O3, O4, O5, O6, O7, O8, O9, O10, O11, O12, O13, O14, O15, O16, O17, O18, O19, O20,
       O21, O22, O23, O24, O25, O26, O27, O28, O29, O30, O31;

  Demultiplexer #(.select(5), .disabled(0)) demultiplexer_1 (
    .out0(_0), .out1(_1), .out2(_2), .out3(_3), .out4(_4), .out5(_5), .out6(_6), .out7(_7), .out8(_8),
    .out9(_9), .out10(_10), .out11(_11), .out12(_12), .out13(_13), .out14(_14), .out15(_15), .out16(_16),
    .out17(_17), .out18(_18), .out19(_19), .out20(_20), .out21(_21), .out22(_22), .out23(_23), .out24(_24),
    .out25(_25), .out26(_26), .out27(_27), .out28(_28), .out29(_29), .out30(_30), .out31(_31), .in(1'b1),
    .sel(A3));  // open: en
  Register #(.width(32)) register_1 (.D(WD), .en(and_1_out), .Q(O0), .clk(clk), .clr(reset));
  and and_1 (and_1_out, _0, WE);
  Register #(.width(32)) register_2 (.D(WD), .en(and_2_out), .Q(O4), .clk(clk), .clr(reset));
  and and_2 (and_2_out, _4, WE);
  Register #(.width(32)) register_3 (.D(WD), .en(and_3_out), .Q(O8), .clk(clk), .clr(reset));
  and and_3 (and_3_out, _8, WE);
  Register #(.width(32)) register_4 (.D(WD), .en(and_4_out), .Q(O12), .clk(clk), .clr(reset));
  and and_4 (and_4_out, _12, WE);
  Register #(.width(32)) register_5 (.D(WD), .en(and_5_out), .Q(O16), .clk(clk), .clr(reset));
  and and_5 (and_5_out, _16, WE);
  Register #(.width(32)) register_6 (.D(WD), .en(and_6_out), .Q(O20), .clk(clk), .clr(reset));
  and and_6 (and_6_out, _20, WE);
  Register #(.width(32)) register_7 (.D(WD), .en(and_7_out), .Q(O24), .clk(clk), .clr(reset));
  and and_7 (and_7_out, _24, WE);
  Register #(.width(32)) register_8 (.D(WD), .en(and_8_out), .Q(O28), .clk(clk), .clr(reset));
  and and_8 (and_8_out, _28, WE);
  and and_9 (and_9_out, _1, WE);
  and and_10 (and_10_out, _5, WE);
  and and_11 (and_11_out, _9, WE);
  and and_12 (and_12_out, _13, WE);
  and and_13 (and_13_out, _17, WE);
  and and_14 (and_14_out, _21, WE);
  and and_15 (and_15_out, _25, WE);
  and and_16 (and_16_out, _29, WE);
  Register #(.width(32)) register_9 (.D(WD), .en(and_9_out), .Q(O1), .clk(clk), .clr(reset));
  Register #(.width(32)) register_10 (.D(WD), .en(and_10_out), .Q(O5), .clk(clk), .clr(reset));
  Register #(.width(32)) register_11 (.D(WD), .en(and_11_out), .Q(O9), .clk(clk), .clr(reset));
  Register #(.width(32)) register_12 (.D(WD), .en(and_12_out), .Q(O13), .clk(clk), .clr(reset));
  Register #(.width(32)) register_13 (.D(WD), .en(and_13_out), .Q(O17), .clk(clk), .clr(reset));
  Register #(.width(32)) register_14 (.D(WD), .en(and_14_out), .Q(O21), .clk(clk), .clr(reset));
  Register #(.width(32)) register_15 (.D(WD), .en(and_15_out), .Q(O25), .clk(clk), .clr(reset));
  Register #(.width(32)) register_16 (.D(WD), .en(and_16_out), .Q(O29), .clk(clk), .clr(reset));
  and and_17 (and_17_out, _2, WE);
  and and_18 (and_18_out, _6, WE);
  and and_19 (and_19_out, _10, WE);
  and and_20 (and_20_out, _14, WE);
  and and_21 (and_21_out, _18, WE);
  and and_22 (and_22_out, _22, WE);
  and and_23 (and_23_out, _26, WE);
  and and_24 (and_24_out, _30, WE);
  Register #(.width(32)) register_17 (.D(WD), .en(and_17_out), .Q(O2), .clk(clk), .clr(reset));
  Register #(.width(32)) register_18 (.D(WD), .en(and_18_out), .Q(O6), .clk(clk), .clr(reset));
  Register #(.width(32)) register_19 (.D(WD), .en(and_19_out), .Q(O10), .clk(clk), .clr(reset));
  Register #(.width(32)) register_20 (.D(WD), .en(and_20_out), .Q(O14), .clk(clk), .clr(reset));
  Register #(.width(32)) register_21 (.D(WD), .en(and_21_out), .Q(O18), .clk(clk), .clr(reset));
  Register #(.width(32)) register_22 (.D(WD), .en(and_22_out), .Q(O22), .clk(clk), .clr(reset));
  Register #(.width(32)) register_23 (.D(WD), .en(and_23_out), .Q(O26), .clk(clk), .clr(reset));
  Register #(.width(32)) register_24 (.D(WD), .en(and_24_out), .Q(O30), .clk(clk), .clr(reset));
  Register #(.width(32)) register_25 (.D(WD), .en(and_25_out), .Q(O3), .clk(clk), .clr(reset));
  and and_25 (and_25_out, _3, WE);
  Register #(.width(32)) register_26 (.D(WD), .en(and_26_out), .Q(O7), .clk(clk), .clr(reset));
  and and_26 (and_26_out, _7, WE);
  Register #(.width(32)) register_27 (.D(WD), .en(and_27_out), .Q(O11), .clk(clk), .clr(reset));
  and and_27 (and_27_out, _11, WE);
  Register #(.width(32)) register_28 (.D(WD), .en(and_28_out), .Q(O15), .clk(clk), .clr(reset));
  and and_28 (and_28_out, _15, WE);
  Register #(.width(32)) register_29 (.D(WD), .en(and_29_out), .Q(O19), .clk(clk), .clr(reset));
  and and_29 (and_29_out, _19, WE);
  Register #(.width(32)) register_30 (.D(WD), .en(and_30_out), .Q(O23), .clk(clk), .clr(reset));
  and and_30 (and_30_out, _23, WE);
  Register #(.width(32)) register_31 (.D(WD), .en(and_31_out), .Q(O27), .clk(clk), .clr(reset));
  and and_31 (and_31_out, _27, WE);
  Register #(.width(32)) register_32 (.D(WD), .en(and_32_out), .Q(O31), .clk(clk), .clr(reset));
  and and_32 (and_32_out, _31, WE);
  Multiplexer #(.select(5), .width(32)) multiplexer_1 (
    .in0({32{1'b0}}), .in1(O1), .in2(O2), .in3(O3), .in4(O4), .in5(O5), .in6(O6), .in7(O7), .in8(O8),
    .in9(O9), .in10(O10), .in11(O11), .in12(O12), .in13(O13), .in14(O14), .in15(O15), .in16(O16), .in17(O17),
    .in18(O18), .in19(O19), .in20(O20), .in21(O21), .in22(O22), .in23(O23), .in24(O24), .in25(O25),
    .in26(O26), .in27(O27), .in28(O28), .in29(O29), .in30(O30), .in31(O31), .out(RD1), .sel(A1));  // open: en
  Multiplexer #(.select(5), .width(32)) multiplexer_2 (
    .in0({32{1'b0}}), .in1(O1), .in2(O2), .in3(O3), .in4(O4), .in5(O5), .in6(O6), .in7(O7), .in8(O8),
    .in9(O9), .in10(O10), .in11(O11), .in12(O12), .in13(O13), .in14(O14), .in15(O15), .in16(O16), .in17(O17),
    .in18(O18), .in19(O19), .in20(O20), .in21(O21), .in22(O22), .in23(O23), .in24(O24), .in25(O25),
    .in26(O26), .in27(O27), .in28(O28), .in29(O29), .in30(O30), .in31(O31), .out(RD2), .sel(A2));  // open: en
endmodule
