// Logisim project pipelineCycle_Appearance.circ as structural Verilog
module main (
  input  in_1
);

  wire ALUSrcD, BranchConditionD, clk, MemWriteD, not_1_out, RegWriteD, SignImmD;
  wire [1:0] TNewD, TuseD;
  wire [2:0] ALUControlD, PCSrcD, RD1ForwardD, RD1ForwardE, RD2ForwardD, RD2ForwardE, RegDataSrcD, RegDstD;
  wire [4:0] _15_11D, _15_11E, _20_16D, _20_16E, _25_21D, RegAddrE, WriteRegE, WriteRegW;
  wire [5:0] _5_0D, _31_26D;
  wire [15:0] _15_0D;
  wire [25:0] _25_0D;
  wire [31:0] ALUResultE, ALUResultM, ALUResultW, bit_extender_1_out, bit_extender_2_out, Imm32D, Imm32E,
       Imm32toIFUF, InstrD, InstrF, MemoryDataM, MemoryDataW, PCPlus8E, PCPlus8F, PCPlus8M, PCPlus8W, RD1D,
       RD1E, RD1ForwardResultD, RD1ForwardResultE, RD2D, RD2E, RD2ForwardResulD, RD2ForwardResultE,
       RD2ForwardResultM, RegData, RegDataW, SrcBE;

  Multiplexer #(.width(32)) multiplexer_1 (
    .in0(32'h1), .in1(Imm32D), .out(Imm32toIFUF), .sel(BranchConditionD));  // open: en
  Clock clock_1 (.out(clk));
  IFU ifu_1 (
    .Imm32(Imm32toIFUF), .rst(in_1), .Instr(InstrF), .PCPlus8(PCPlus8F), .PCSrc(PCSrcD), .clk(clk),
    ._25_0(_25_0D), .RD1(RD1ForwardResultD));
  pipelineRegister pipelineregister_1 ();
  splitter splitter_1 (
    .Instr(InstrD), ._31_26(_31_26D), ._5_0(_5_0D), ._25_21(_25_21D), ._20_16(_20_16D), ._15_11(_15_11D),
    ._15_0(_15_0D), ._25_0(_25_0D));
  assign bit_extender_1_out = {{16{1'b0}}, _15_0D};  // Bit_Extender bit_extender_1
  assign bit_extender_2_out = {{16{_15_0D[15]}}, _15_0D};  // Bit_Extender bit_extender_2
  Multiplexer #(.width(32)) multiplexer_2 (
    .in0(bit_extender_1_out), .in1(bit_extender_2_out), .out(Imm32D), .sel(SignImmD));  // open: en
  // ControlUnit controlunit_1: pin names not known; wires that end beside it: InstrD, BranchConditionD, _31_26D, _5_0D, RegDataSrcD, MemWriteD, PCSrcD, ALUSrcD, RegDstD, RegWriteD, ALUControlD, SignImmD, TuseD, TNewD
  GRF grf_1 (
    .A1(_25_21D), .A2(_20_16D), .A3(WriteRegW), .WD(RegDataW), .RD1(RD1D), .RD2(RD2D), .reset(in_1),
    .WE(RegWriteD), .clk(clk));
  Multiplexer #(.select(3), .width(32)) multiplexer_3 (
    .in0(RD1D), .in1(PCPlus8E), .in2(ALUResultM), .in3(PCPlus8M), .out(RD1ForwardResultD), .sel(RD1ForwardD));  // open: in4, in5, in6, in7, en
  Multiplexer #(.select(3), .width(32)) multiplexer_4 (
    .in0(RD2D), .in1(PCPlus8E), .in2(ALUResultM), .in3(PCPlus8M), .out(RD2ForwardResulD), .sel(RD2ForwardD));  // open: in4, in5, in6, in7, en
  Comparator #(.width(32)) comparator_1 (
    .a(RD1ForwardResultD), .b(RD2ForwardResulD), .eq(BranchConditionD));  // open: gt, lt
  pipelineRegister pipelineregister_2 ();
  Multiplexer #(.select(3), .width(32)) multiplexer_5 (
    .in0(RD1E), .in1(ALUResultM), .in2(PCPlus8M), .in7(RegData), .out(RD1ForwardResultE), .sel(RD1ForwardE));  // open: in3, in4, in5, in6, en
  Multiplexer #(.select(3), .width(32)) multiplexer_6 (
    .in0(RD2E), .in1(ALUResultM), .in2(PCPlus8M), .in7(RegDataW), .out(RD2ForwardResultE), .sel(RD2ForwardE));  // open: in3, in4, in5, in6, en
  Multiplexer #(.select(3), .width(5)) multiplexer_7 (
    .in0(_20_16E), .in1(_15_11E), .in2({5{1'b1}}), .out(RegAddrE), .sel(RegDstD));  // open: in3, in4, in5, in6, in7, en
  HazardUnit hazardunit_1 ();
  Multiplexer #(.width(32)) multiplexer_8 (
    .in0(RD2ForwardResultE), .in1(Imm32E), .out(SrcBE), .sel(ALUSrcD));  // open: en
  Multiplexer #(.width(5)) multiplexer_9 (
    .in0({5{1'b0}}), .in1(RegAddrE), .out(WriteRegE), .sel(RegWriteD));  // open: en
  ALU alu_1 (.SrcA(RD1ForwardResultE), .SrcB(SrcBE), .ALUResult(ALUResultE), .ALUControl(ALUControlD));  // open: Zero
  pipelineRegister pipelineregister_3 ();
  RAM #(.addrWidth(5), .dataWidth(32), .bus("separate")) ram_1 (
    .addr(ALUResultM[6:2]), .din(RD2ForwardResultM), .data(MemoryDataM), .str(MemWriteD), .clk(clk),
    .ld(not_1_out), .clr(in_1));  // open: sel
  not not_1 (not_1_out, MemWriteD);
  pipelineRegister pipelineregister_4 ();
  Multiplexer #(.select(3), .width(32)) multiplexer_10 (
    .in0(ALUResultW), .in1(MemoryDataW), .in2(PCPlus8W), .out(RegDataW), .sel(RegDataSrcD));  // open: in3, in4, in5, in6, in7, en

  // Other names for the same wires on the sheet: ALUControlE[2:0] = ALUControlD; ALUSrcE = ALUSrcD;
  //   MemWriteE = MemWriteD; MemWriteM = MemWriteD; RegDataSrcE[2:0] = RegDataSrcD; RegDataSrcM[2:0] = RegDataSrcD;
  //   RegDataSrcW[2:0] = RegDataSrcD; RegDstE[2:0] = RegDstD; RegWriteE = RegWriteD; RegWriteM = RegWriteD;
  //   RegWriteW = RegWriteD; rst = in_1; TNewE[1:0] = TNewD; TNewM[1:0] = TNewD; TNewW[1:0] = TNewD

  // Notes on the sheet:
  //   F
  //   D
  //   E
  //   M
  //   W
endmodule

module IFU (
  input  clk,
  input  rst,
  input  [2:0] PCSrc,
  input  [31:0] Imm32,
  input  [25:0] _25_0,
  input  [31:0] RD1,
  output [31:0] Instr,
  output [31:0] PCPlus8
);

  wire [27:0] bit_extender_1_out, PCPlus4;
  wire [31:0] multiplexer_1_out, PC, PCBranch, PCJump, shifter_1_out;

  assign bit_extender_1_out = {{2{1'b0}}, _25_0};  // Bit_Extender bit_extender_1
  Shifter #(.width(32)) shifter_1 (.in(Imm32), .\dist (5'b00010), .out(shifter_1_out));
  Shifter #(.width(28)) shifter_2 (.in(bit_extender_1_out), .\dist (5'b00010), .out(PCJump[27:0]));
  Adder #(.width(32)) adder_1 (.a(shifter_1_out), .b(PC), .out(PCBranch));  // open: cin, cout
  Multiplexer #(.select(3), .width(32)) multiplexer_1 (
    .in0({PCJump[31:28], PCPlus4}), .in1(PCBranch), .in2(PCJump), .in3(RD1), .out(multiplexer_1_out),
    .sel(PCSrc));  // open: in4, in5, in6, in7, en
  Register #(.width(32)) register_1 (.D(multiplexer_1_out), .Q(PC), .clk(clk), .clr(rst));  // open: en
  Adder #(.width(32)) adder_2 (.a(PC), .b(32'h4), .out({PCJump[31:28], PCPlus4}));  // open: cin, cout
  ROM #(.addrWidth(5), .dataWidth(32)) rom_1 (.addr(PC[6:2]), .data(Instr));  // open: sel
  Adder #(.width(32)) adder_3 (.a({PCJump[31:28], PCPlus4}), .b(32'h4), .out(PCPlus8));  // open: cin, cout

  // Other names for the same wires on the sheet: PCPlus4[31:28] = PCJump[31:28]; PCReg[31:0] = RD1

  // Notes on the sheet:
  //   contents of rom_1 (hex, n*v repeats v):
  //   3c110064 3c1200c8 c000c04 291a020 2329820 3e00008
endmodule

module splitter (
  input  [31:0] Instr,
  output [5:0] _31_26,
  output [5:0] _5_0,
  output [4:0] _25_21,
  output [4:0] _20_16,
  output [4:0] _15_11,
  output [15:0] _15_0,
  output [25:0] _25_0
);


  assign _5_0 = Instr[5:0];
  assign _15_0 = Instr[15:0];
  assign _15_11 = Instr[15:11];
  assign _20_16 = Instr[20:16];
  assign _25_0 = Instr[25:0];
  assign _25_21 = Instr[25:21];
  assign _31_26 = Instr[31:26];
endmodule

module GRF (
  input  clk,
  input  reset,
  input  WE,
  input  [4:0] A1,
  input  [4:0] A2,
  input  [4:0] A3,
  input  [31:0] WD,
  output [31:0] RD1,
  output [31:0] RD2
);

  wire _0, _1, _2, _3, _4, _5, _6, _7, _8, _9, _10, _11, _12, _13, _14, _15, _16, _17, _18, _19, _20, _21,
       _22, _23, _24, _25, _26, _27, _28, _29, _30, _31, and_1_out, and_2_out, and_3_out, and_4_out,
       and_5_out, and_6_out, and_7_out, and_8_out, and_9_out, and_10_out, and_11_out, and_12_out, and_13_out,
       and_14_out, and_15_out, and_16_out, and_17_out, and_18_out, and_19_out, and_20_out, and_21_out,
       and_22_out, and_23_out, and_24_out, and_25_out, and_26_out, and_27_out, and_28_out, and_29_out,
       and_30_out, and_31_out, and_32_out;
  wire [31:0] O0, O1, O2, O3, O4, O5, O6, O7, O8, O9, O10, O11, O12, O13, O14, O15, O16, O17, O18, O19, O20,
       O21, O22, O23, O24, O25, O26, O27, O28, O29, O30, O31;

  Demultiplexer #(.select(5), .disabled(0)) demultiplexer_1 (
    .out0(_0), .out1(_1), .out2(_2), .out3(_3), .out4(_4), .out5(_5), .out6(_6), .out7(_7), .out8(_8),
    .out9(_9), .out10(_10), .out11(_11), .out12(_12), .out13(_13), .out14(_14), .out15(_15), .out16(_16),
    .out17(_17), .out18(_18), .out19(_19), .out20(_20), .out21(_21), .out22(_22), .out23(_23), .out24(_24),
    .out25(_25), .out26(_26), .out27(_27), .out28(_28), .out29(_29), .out30(_30), .out31(_31), .in(1'b1),
    .sel(A3));  // open: en
  Register #(.width(32)) register_1 (.D(WD), .en(and_1_out), .Q(O0), .clk(clk), .clr(reset));
  and and_1 (and_1_out, _0, WE);
  Register #(.width(32)) register_2 (.D(WD), .en(and_2_out), .Q(O4), .clk(clk), .clr(reset));
  and and_2 (and_2_out, _4, WE);
  Register #(.width(32)) register_3 (.D(WD), .en(and_3_out), .Q(O8), .clk(clk), .clr(reset));
  and and_3 (and_3_out, _8, WE);
  Register #(.width(32)) register_4 (.D(WD), .en(and_4_out), .Q(O12), .clk(clk), .clr(reset));
  and and_4 (and_4_out, _12, WE);
  Register #(.width(32)) register_5 (.D(WD), .en(and_5_out), .Q(O16), .clk(clk), .clr(reset));
  and and_5 (and_5_out, _16, WE);
  Register #(.width(32)) register_6 (.D(WD), .en(and_6_out), .Q(O20), .clk(clk), .clr(reset));
  and and_6 (and_6_out, _20, WE);
  Register #(.width(32)) register_7 (.D(WD), .en(and_7_out), .Q(O24), .clk(clk), .clr(reset));
  and and_7 (and_7_out, _24, WE);
  Register #(.width(32)) register_8 (.D(WD), .en(and_8_out), .Q(O28), .clk(clk), .clr(reset));
  and and_8 (and_8_out, _28, WE);
  and and_9 (and_9_out, _1, WE);
  and and_10 (and_10_out, _5, WE);
  and and_11 (and_11_out, _9, WE);
  and and_12 (and_12_out, _13, WE);
  and and_13 (and_13_out, _17, WE);
  and and_14 (and_14_out, _21, WE);
  and and_15 (and_15_out, _25, WE);
  and and_16 (and_16_out, _29, WE);
  Register #(.width(32)) register_9 (.D(WD), .en(and_9_out), .Q(O1), .clk(clk), .clr(reset));
  Register #(.width(32)) register_10 (.D(WD), .en(and_10_out), .Q(O5), .clk(clk), .clr(reset));
  Register #(.width(32)) register_11 (.D(WD), .en(and_11_out), .Q(O9), .clk(clk), .clr(reset));
  Register #(.width(32)) register_12 (.D(WD), .en(and_12_out), .Q(O13), .clk(clk), .clr(reset));
  Register #(.width(32)) register_13 (.D(WD), .en(and_13_out), .Q(O17), .clk(clk), .clr(reset));
  Register #(.width(32)) register_14 (.D(WD), .en(and_14_out), .Q(O21), .clk(clk), .clr(reset));
  Register #(.width(32)) register_15 (.D(WD), .en(and_15_out), .Q(O25), .clk(clk), .clr(reset));
  Register #(.width(32)) register_16 (.D(WD), .en(and_16_out), .Q(O29), .clk(clk), .clr(reset));
  and and_17 (and_17_out, _2, WE);
  and and_18 (and_18_out, _6, WE);
  and and_19 (and_19_out, _10, WE);
  and and_20 (and_20_out, _14, WE);
  and and_21 (and_21_out, _18, WE);
  and and_22 (and_22_out, _22, WE);
  and and_23 (and_23_out, _26, WE);
  and and_24 (and_24_out, _30, WE);
  Register #(.width(32)) register_17 (.D(WD), .en(and_17_out), .Q(O2), .clk(clk), .clr(reset));
  Register #(.width(32)) register_18 (.D(WD), .en(and_18_out), .Q(O6), .clk(clk), .clr(reset));
  Register #(.width(32)) register_19 (.D(WD), .en(and_19_out), .Q(O10), .clk(clk), .clr(reset));
  Register #(.width(32)) register_20 (.D(WD), .en(and_20_out), .Q(O14), .clk(clk), .clr(reset));
  Register #(.width(32)) register_21 (.D(WD), .en(and_21_out), .Q(O18), .clk(clk), .clr(reset));
  Register #(.width(32)) register_22 (.D(WD), .en(and_22_out), .Q(O22), .clk(clk), .clr(reset));
  Register #(.width(32)) register_23 (.D(WD), .en(and_23_out), .Q(O26), .clk(clk), .clr(reset));
  Register #(.width(32)) register_24 (.D(WD), .en(and_24_out), .Q(O30), .clk(clk), .clr(reset));
  and and_25 (and_25_out, _3, WE);
  and and_26 (and_26_out, _7, WE);
  and and_27 (and_27_out, _11, WE);
  and and_28 (and_28_out, _15, WE);
  and and_29 (and_29_out, _19, WE);
  and and_30 (and_30_out, _23, WE);
  and and_31 (and_31_out, _27, WE);
  and and_32 (and_32_out, _31, WE);
  Register #(.width(32)) register_25 (.D(WD), .en(and_25_out), .Q(O3), .clk(clk), .clr(reset));
  Register #(.width(32)) register_26 (.D(WD), .en(and_26_out), .Q(O7), .clk(clk), .clr(reset));
  Register #(.width(32)) register_27 (.D(WD), .en(and_27_out), .Q(O11), .clk(clk), .clr(reset));
  Register #(.width(32)) register_28 (.D(WD), .en(and_28_out), .Q(O15), .clk(clk), .clr(reset));
  Register #(.width(32)) register_29 (.D(WD), .en(and_29_out), .Q(O19), .clk(clk), .clr(reset));
  Register #(.width(32)) register_30 (.D(WD), .en(and_30_out), .Q(O23), .clk(clk), .clr(reset));
  Register #(.width(32)) register_31 (.D(WD), .en(and_31_out), .Q(O27), .clk(clk), .clr(reset));
  Register #(.width(32)) register_32 (.D(WD), .en(and_32_out), .Q(O31), .clk(clk), .clr(reset));
  Multiplexer #(.select(5), .width(32)) multiplexer_1 (
    .in0({32{1'b0}}), .in1(O1), .in2(O2), .in3(O3), .in4(O4), .in5(O5), .in6(O6), .in7(O7), .in8(O8),
    .in9(O9), .in10(O10), .in11(O11), .in12(O12), .in13(O13), .in14(O14), .in15(O15), .in16(O16), .in17(O17),
    .in18(O18), .in19(O19), .in20(O20), .in21(O21), .in22(O22), .in23(O23), .in24(O24), .in25(O25),
    .in26(O26), .in27(O27), .in28(O28), .in29(O29), .in30(O30), .in31(O31), .out(RD1), .sel(A1));  // open: en
  Multiplexer #(.select(5), .width(32)) multiplexer_2 (
    .in0({32{1'b0}}), .in1(O1), .in2(O2), .in3(O3), .in4(O4), .in5(O5), .in6(O6), .in7(O7), .in8(O8),
    .in9(O9), .in10(O10), .in11(O11), .in12(O12), .in13(O13), .in14(O14), .in15(O15), .in16(O16), .in17(O17),
    .in18(O18), .in19(O19), .in20(O20), .in21(O21), .in22(O22), .in23(O23), .in24(O24), .in25(O25),
    .in26(O26), .in27(O27), .in28(O28), .in29(O29), .in30(O30), .in31(O31), .out(RD2), .sel(A2));  // open: en
endmodule

module ALU (
  input  [31:0] SrcA,
  input  [2:0] ALUControl,
  input  [31:0] SrcB,
  output Zero,
  output [31:0] ALUResult
);

  wire [31:0] adder_1_out, AND_out, OR_out, shifter_1_out, subtractor_1_out;

  Adder #(.width(32)) adder_1 (.a(SrcA), .b(SrcB), .out(adder_1_out));  // open: cin, cout
  Subtractor #(.width(32)) subtractor_1 (.a(SrcA), .b(SrcB), .out(subtractor_1_out));  // open: bin, bout
  assign AND_out = SrcA & SrcB;  // AND_Gate AND, 32 bits wide
  assign OR_out = SrcA | SrcB;  // OR_Gate OR, 32 bits wide
  Shifter #(.width(32)) shifter_1 (.in(SrcB), .\dist (5'b10000), .out(shifter_1_out));
  Multiplexer #(.select(3), .width(32)) multiplexer_1 (
    .in0(adder_1_out), .in1(subtractor_1_out), .in2(AND_out), .in3(OR_out), .in4(shifter_1_out),
    .out(ALUResult), .sel(ALUControl));  // open: in5, in6, in7, en
  Comparator #(.width(32)) comparator_1 (.a({32{1'b0}}), .b(ALUResult), .eq(Zero));  // open: gt, lt
endmodule

module ControlUnit (
  input  Zero,
  input  [5:0] Opcode,
  input  [5:0] Funct,
  input  [31:0] Instr,
  output [2:0] out_5,
  output out_6,
  output [2:0] out_7,
  output out_8,
  output [2:0] out_9,
  output out_10,
  output out_11,
  output [1:0] out_12,
  output [1:0] out_13,
  output [2:0] out_14
);

  wire [2:0] controlunit_maindecoder_1_out_5;

  ControlUnit_MainDecoder controlunit_maindecoder_1 (
    .Opcode(Opcode), .out_5(controlunit_maindecoder_1_out_5), .out_7(out_6), .out_9(out_8), .out_11(out_10),
    .out_12(out_11), .out_6(out_5), .out_8(out_7), .Funct(Funct), .out_10(out_9), .Zero(Zero),
    .out_13(out_12), .out_14(out_13));  // open: Instr
  ControlUnit_ALUDecoder controlunit_aludecoder_1 (
    .ALUOP(controlunit_maindecoder_1_out_5), .Funct(Funct), .ALUControl(out_14));
endmodule

module ControlUnit_ALUDecoder (
  input  [5:0] Funct,
  input  [2:0] ALUOP,
  output [2:0] ALUControl
);

  wire comparator_1_eq, comparator_2_eq;
  wire [2:0] Funct_out, multiplexer_1_out, multiplexer_2_out, multiplexer_3_out;

  Multiplexer #(.width(3)) multiplexer_1 (.in0(3'b000), .in1(3'b000), .out(multiplexer_1_out), .sel(1'b1));  // open: en
  Comparator #(.width(6)) comparator_1 (.a(Funct), .b(6'b100000), .eq(comparator_1_eq));  // open: gt, lt
  Multiplexer #(.width(3)) multiplexer_2 (
    .in0(3'b000), .in1(3'b000), .out(multiplexer_2_out), .sel(comparator_1_eq));  // open: en
  Comparator #(.width(6)) comparator_2 (.a(Funct), .b(6'b100010), .eq(comparator_2_eq));  // open: gt, lt
  Multiplexer #(.width(3)) multiplexer_3 (
    .in0(3'b000), .in1(3'b001), .out(multiplexer_3_out), .sel(comparator_2_eq));  // open: en
  assign Funct_out = multiplexer_1_out | multiplexer_2_out | multiplexer_3_out;  // OR_Gate Funct, 3 bits wide
  Multiplexer #(.select(3), .width(3)) multiplexer_4 (
    .in0(Funct_out), .in1(3'b011), .in2(3'b000), .in3(3'b001), .in4(3'b100), .out(ALUControl), .sel(ALUOP));  // open: in5, in6, in7, en

  // Notes on the sheet:
  //   Default
endmodule

module ControlUnit_MainDecoder (
  input  Zero,
  input  [5:0] Funct,
  input  [5:0] Opcode,
  input  [31:0] Instr,
  output [2:0] out_5,
  output [2:0] out_6,
  output out_7,
  output [2:0] out_8,
  output out_9,
  output [2:0] out_10,
  output out_11,
  output out_12,
  output [1:0] out_13,
  output [1:0] out_14
);

  wire BEQ_out, comparator_1_eq, JAL_out, JR_out, LUI_out, LW_out, not_1_out, not_2_out, not_3_out,
       not_4_out, not_5_out, not_6_out, ORI_out, R_Type, SW_out, undriven, undriven_2, undriven_3,
       undriven_4, undriven_5, undriven_6, undriven_7, undriven_8;

  not not_1 (not_1_out, Opcode[4]);
  not not_2 (not_2_out, Opcode[5]);
  not not_3 (not_3_out, Opcode[3]);
  not not_4 (not_4_out, Opcode[2]);
  not not_5 (not_5_out, Opcode[0]);
  not not_6 (not_6_out, Opcode[1]);
  and u_R_Type (R_Type, not_2_out, not_1_out, not_3_out, not_4_out, not_6_out, not_5_out);
  and ORI (ORI_out, not_2_out, not_1_out, Opcode[3], Opcode[2], not_6_out, Opcode[0]);
  and LW (LW_out, Opcode[5], not_1_out, not_3_out, not_4_out, Opcode[1], Opcode[0]);
  and SW (SW_out, Opcode[5], not_1_out, Opcode[3], not_4_out, Opcode[1], Opcode[0]);
  and BEQ (BEQ_out, not_2_out, not_1_out, not_3_out, Opcode[2], not_6_out, not_5_out);
  and LUI (LUI_out, not_2_out, not_1_out, Opcode[3], Opcode[2], Opcode[1], Opcode[0]);
  and JAL (JAL_out, not_2_out, not_1_out, not_3_out, not_4_out, Opcode[1], Opcode[0]);
  Comparator #(.width(6)) comparator_1 (.a(Funct), .b(6'b001000), .eq(comparator_1_eq));  // open: gt, lt
  and JR (JR_out, comparator_1_eq, R_Type);
  // AND_Gate NOP is placed but not wired
  ControlUnit_MainDecoder_ALUOPDecoder controlunit_maindecoder_aluopdecoder_1 (
    .R_Type(R_Type), .ORI(ORI_out), .LW(LW_out), .SW(SW_out), .BEQ(BEQ_out), .LUI(LUI_out), .ALUOP(out_5));
  ControlUnit_MainDecoder_RegDataSrcDecoder controlunit_maindecoder_regdatasrcdecoder_1 (
    .LW(LW_out), .JAL(JAL_out), .RegDataSrc(out_6));
  buf MemWrite (out_7, SW_out);  // OR_Gate
  or ALUSrc (out_9, ORI_out, LW_out, SW_out, LUI_out);
  ControlUnit_MainDecoder_RegDstDecoder controlunit_maindecoder_regdstdecoder_1 (
    .R_Type(R_Type), .JAL(JAL_out), .out_3(out_10));
  or RegWrite (out_11, R_Type, ORI_out, LW_out, LUI_out, JAL_out);
  or SignImm (out_12, LW_out, SW_out, BEQ_out);
  ControlUnit_MainDecoder_TimeDecoder controlunit_maindecoder_timedecoder_1 (
    .in_1(undriven), .in_2(undriven_2), .in_3(undriven_3), .in_4(undriven_4), .in_5(undriven_5),
    .in_6(undriven_6), .in_7(undriven_7), .in_8(undriven_8), .Tuse(out_13), .TnewD(out_14));
  ControlUnit_MainDecoder_PCSrcDecoder controlunit_maindecoder_pcsrcdecoder_1 (
    .BEQ(BEQ_out), .JAL(JAL_out), .out_5(out_8), .JR(JR_out), .Zero(Zero));
endmodule

module ControlUnit_MainDecoder_ALUOPDecoder (
  input  R_Type,
  input  ORI,
  input  LW,
  input  SW,
  input  BEQ,
  input  LUI,
  output [2:0] ALUOP
);

  wire [2:0] multiplexer_1_out, multiplexer_2_out, multiplexer_3_out, multiplexer_4_out, multiplexer_5_out,
       multiplexer_6_out;

  Multiplexer #(.width(3)) multiplexer_1 (
    .in0(3'b000), .in1(3'b000), .out(multiplexer_1_out), .sel(R_Type));  // open: en
  Multiplexer #(.width(3)) multiplexer_2 (.in0(3'b000), .in1(3'b001), .out(multiplexer_2_out), .sel(ORI));  // open: en
  Multiplexer #(.width(3)) multiplexer_3 (.in0(3'b000), .in1(3'b010), .out(multiplexer_3_out), .sel(LW));  // open: en
  Multiplexer #(.width(3)) multiplexer_4 (.in0(3'b000), .in1(3'b010), .out(multiplexer_4_out), .sel(SW));  // open: en
  Multiplexer #(.width(3)) multiplexer_5 (.in0(3'b000), .in1(3'b011), .out(multiplexer_5_out), .sel(BEQ));  // open: en
  Multiplexer #(.width(3)) multiplexer_6 (.in0(3'b000), .in1(3'b100), .out(multiplexer_6_out), .sel(LUI));  // open: en
  assign ALUOP = multiplexer_1_out | multiplexer_2_out | multiplexer_3_out | multiplexer_4_out | multiplexer_5_out | multiplexer_6_out;  // OR_Gate ALUOP, 3 bits wide
endmodule

module ControlUnit_MainDecoder_RegDataSrcDecoder (
  input  LW,
  input  JAL,
  output [2:0] RegDataSrc
);

  wire [2:0] multiplexer_1_out, multiplexer_2_out, multiplexer_3_out;

  Multiplexer #(.width(3)) multiplexer_1 (.in0(3'b000), .in1(3'b000), .out(multiplexer_1_out), .sel(1'b1));  // open: en
  Multiplexer #(.width(3)) multiplexer_2 (.in0(3'b000), .in1(3'b001), .out(multiplexer_2_out), .sel(LW));  // open: en
  Multiplexer #(.width(3)) multiplexer_3 (.in0(3'b000), .in1(3'b010), .out(multiplexer_3_out), .sel(JAL));  // open: en
  assign RegDataSrc = multiplexer_1_out | multiplexer_2_out | multiplexer_3_out;  // OR_Gate MemtoReg, 3 bits wide

  // Notes on the sheet:
  //   Default
endmodule

module ControlUnit_MainDecoder_PCSrcDecoder (
  input  Zero,
  input  BEQ,
  input  JAL,
  input  JR,
  output [2:0] out_5
);

  wire [2:0] multiplexer_1_out, multiplexer_2_out, multiplexer_3_out, multiplexer_4_out;

  Multiplexer #(.width(3)) multiplexer_1 (.in0(3'b000), .in1(3'b000), .out(multiplexer_1_out), .sel(1'b1));  // open: en
  Multiplexer #(.width(3)) multiplexer_2 (.in0(3'b000), .in1(3'b001), .out(multiplexer_2_out), .sel(BEQ));  // open: en
  Multiplexer #(.width(3)) multiplexer_3 (.in0(3'b000), .in1(3'b010), .out(multiplexer_3_out), .sel(JAL));  // open: en
  Multiplexer #(.width(3)) multiplexer_4 (.in0(3'b000), .in1(3'b011), .out(multiplexer_4_out), .sel(JR));  // open: en
  assign out_5 = multiplexer_1_out | multiplexer_2_out | multiplexer_3_out | multiplexer_4_out;  // OR_Gate PCSrc, 3 bits wide

  // Notes on the sheet:
  //   Default
endmodule

module ControlUnit_MainDecoder_RegDstDecoder (
  input  R_Type,
  input  JAL,
  output [2:0] out_3
);

  wire [2:0] multiplexer_1_out, multiplexer_2_out, multiplexer_3_out;

  Multiplexer #(.width(3)) multiplexer_1 (.in0(3'b000), .in1(3'b000), .out(multiplexer_1_out), .sel(1'b1));  // open: en
  Multiplexer #(.width(3)) multiplexer_2 (
    .in0(3'b000), .in1(3'b001), .out(multiplexer_2_out), .sel(R_Type));  // open: en
  Multiplexer #(.width(3)) multiplexer_3 (.in0(3'b000), .in1(3'b010), .out(multiplexer_3_out), .sel(JAL));  // open: en
  assign out_3 = multiplexer_1_out | multiplexer_2_out | multiplexer_3_out;  // OR_Gate RegDst, 3 bits wide

  // Notes on the sheet:
  //   Default
endmodule

module ControlUnit_MainDecoder_TimeDecoder (
  input  in_1,
  input  in_2,
  input  in_3,
  input  in_4,
  input  in_5,
  input  in_6,
  input  in_7,
  input  in_8,
  output [1:0] Tuse,
  output [1:0] TnewD
);
endmodule
